// Logisim project sqrt2.circ as structural Verilog: 45 circuits, main circuit sqrt
module main (
  input  ENABLE,
  input  [15:0] IO_DATA_IN,
  output NAN,
  output PINF,
  output NINF,
  output RESULT,
  output [15:0] IO_DATA_OUT
);

  wire CLK_out;

  Clock CLK (.out(CLK_out));
  sqrt sqrt_1 (
    .CLK(CLK_out), .ENABLE(ENABLE), .IO_DATA_IN(IO_DATA_IN), .IS_NAN(NAN), .IS_PINF(PINF), .IS_NINF(NINF),
    .RESULT(RESULT), .IO_DATA_OUT(IO_DATA_OUT));
endmodule

module sqrt (
  input  CLK,
  input  ENABLE,
  input  [15:0] IO_DATA_IN,
  output IS_NAN,
  output IS_PINF,
  output IS_NINF,
  output RESULT,
  output [15:0] IO_DATA_OUT
);

  wire and_1_out, and_2_out, and_3_out, and_4_out, and_8_out, and_9_out, check_incorrect_inp_1_has_result,
       comp32_1_eq, comp32_1_more, ENABLE_t, if_y_eq_x_1_ans, if_y_eq_x_2_ans, if_y_less_x_1_ans,
       if_y_more_x_1_ans, if_y_more_x_3_ans, if_y_more_x_4_ans, not_1_out, not_2_out, not_4_out, not_13_out,
       not_14_out, not_15_out, not_20_out, or_1_out, or_2_out, or_3_out, or_4_out, RESULT_t, SIGN,
       transmission_3_p2, transmission_4_p2, transmission_4_p3, transmission_5_p3, transmission_8_p3,
       transmission_9_p3, transmission_12_p3, transmission_17_p3, WAS_RESULT_CALC_FIRST_TICK;
  wire [4:0] EXP;
  wire [5:0] CUR_TICK;
  wire [9:0] MANT, transmission_8_p4;
  wire [15:0] check_incorrect_inp_1_out_data, dtrigger16_1_q, OUT_DATA, transmission_1_p1;
  wire [21:0] transmission_8_p4_2;
  wire [31:0] format_mant_and_exp_1_ans_exp, int32_sqrt_algo_1_out_number, NUMBER_FOR_SQRT,
       transmission_4_p4, transmission_14_p3, transmission_15_p3;

  DtriggerOnJK dtriggeronjk_1 (.D(ENABLE), .C(CLK), .Q(ENABLE_t));  // open: NQ
  not not_1 (not_1_out, ENABLE_t);
  IF_y_more_x if_y_more_x_1 (.Y({{26{1'b0}}, CUR_TICK}), .X({32{1'b0}}), .ans(if_y_more_x_1_ans));
  // Probe on transmission_1_p1
  and and_1 (and_1_out, CLK, not_1_out);
  and and_2 (and_2_out, RESULT_t, if_y_more_x_1_ans);
  not not_2 (not_2_out, ENABLE_t);
  or or_1 (or_1_out, and_2_out, not_2_out);
  // Transmission_Gate #(.width(16)) transmission_1: pin names not known; wires that end beside it: transmission_1_p1, ENABLE_t, IO_DATA_IN
  // NOT_Gate not_3 has open pins: in=ENABLE_t, out=open
  DTrigger16 dtrigger16_1 (.D(transmission_1_p1), .C(and_1_out), .Enabled(1'b1), .Q(dtrigger16_1_q));  // open: NQ
  // Probe on {{22{1'b0}}, MANT}
  // Probe on dtrigger16_1_q
  Counter counter_1 (.Enabled(ENABLE_t), .CLK(CLK), .Done(or_1_out), .CUR_TICK(CUR_TICK));
  IF_y_less_x if_y_less_x_1 (.Y({{26{1'b0}}, CUR_TICK}), .X(32'hb), .ans(if_y_less_x_1_ans));
  COMP32 comp32_1 (.A({{26{1'b0}}, CUR_TICK}), .B({32{1'b0}}), .EQ(comp32_1_eq), .MORE(comp32_1_more));  // open: LESS
  not not_4 (not_4_out, ENABLE_t);
  // Transmission_Gate #(.width(16)) transmission_2: pin names not known; wires that end beside it: dtrigger16_1_q, not_4_out, ENABLE_t, {SIGN, EXP, MANT}
  and and_3 (and_3_out, CLK, if_y_less_x_1_ans);
  or or_2 (or_2_out, comp32_1_eq, comp32_1_more);
  // NOT_Gate not_5 has open pins: in=transmission_3_p2, out=open
  // Transmission_Gate #(.width(16)) transmission_3: pin names not known; wires that end beside it: IO_DATA_IN, transmission_3_p2, OUT_DATA
  // Probe on {{26{1'b0}}, CUR_TICK}
  // Transmission_Gate #(.width(32)) transmission_4: pin names not known; wires that end beside it: NUMBER_FOR_SQRT, transmission_4_p2, transmission_4_p3, transmission_4_p4
  not not_6 (transmission_4_p3, transmission_4_p2);
  and and_4 (and_4_out, comp32_1_more, ENABLE_t);
  // Transmission_Gate #(.width(32)) transmission_5: pin names not known; wires that end beside it: {32{1'b0}}, transmission_4_p2, transmission_5_p3, transmission_4_p4
  not not_7 (transmission_5_p3, transmission_4_p2);
  CHECK_INCORRECT_INP check_incorrect_inp_1 (
    .MANT({{22{1'b0}}, MANT}), .EXP({{27{1'b0}}, EXP}), .SIGN(SIGN), .NAN(IS_NAN), .PINF(IS_PINF),
    .NINF(IS_NINF), .HAS_RESULT(check_incorrect_inp_1_has_result), .OUT_DATA(check_incorrect_inp_1_out_data));
  or or_3 (or_3_out, and_4_out, WAS_RESULT_CALC_FIRST_TICK);
  // Probe on OUT_DATA
  // NOT_Gate not_8 has open pins: in=WAS_RESULT_CALC_FIRST_TICK, out=open
  // NOT_Gate not_9 has open pins: in=WAS_RESULT_CALC_FIRST_TICK, out=open
  and and_5 (WAS_RESULT_CALC_FIRST_TICK, check_incorrect_inp_1_has_result, ENABLE_t, or_2_out);
  and and_6 (transmission_3_p2, and_4_out, or_3_out);
  IF_y_more_x if_y_more_x_2 (.Y({{26{1'b0}}, CUR_TICK}), .X({32{1'b0}}), .ans(transmission_4_p2));
  // Transmission_Gate transmission_6: pin names not known; wires that end beside it: check_incorrect_inp_1_has_result, WAS_RESULT_CALC_FIRST_TICK, RESULT_t
  // Transmission_Gate #(.width(16)) transmission_7: pin names not known; wires that end beside it: check_incorrect_inp_1_has_result, check_incorrect_inp_1_out_data, WAS_RESULT_CALC_FIRST_TICK, OUT_DATA
  // Probe on transmission_4_p4
  INT32_SQRT_ALGO int32_sqrt_algo_1 (
    .INP_NUMBER(transmission_4_p4), .CLK(and_3_out), .ENABLE(ENABLE_t), .CUR_TICK({{26{1'b0}}, CUR_TICK}),
    .OUT_NUMBER(int32_sqrt_algo_1_out_number));
  // Transmission_Gate #(.width(32)) transmission_8: pin names not known; wires that end beside it: int32_sqrt_algo_1_out_number, transmission_4_p2, transmission_8_p3, {transmission_8_p4_2, transmission_8_p4}
  not not_10 (transmission_8_p3, transmission_4_p2);
  // Probe on {transmission_8_p4_2, transmission_8_p4}
  // Transmission_Gate #(.width(10)) transmission_9: pin names not known; wires that end beside it: transmission_8_p4, WAS_RESULT_CALC_FIRST_TICK, transmission_9_p3, OUT_DATA[9:0]
  not not_11 (transmission_9_p3, WAS_RESULT_CALC_FIRST_TICK);
  IF_y_more_x if_y_more_x_3 (.Y({{26{1'b0}}, CUR_TICK}), .X({32{1'b0}}), .ans(if_y_more_x_3_ans));
  // Probe on {{26{1'b0}}, CUR_TICK}
  and and_7 (RESULT, RESULT_t, if_y_more_x_3_ans);
  // Transmission_Gate transmission_10: pin names not known; wires that end beside it: 1'b0, ENABLE_t, RESULT_t
  // NOT_Gate not_12 has open pins: in=ENABLE_t, out=open
  not not_13 (not_13_out, WAS_RESULT_CALC_FIRST_TICK);
  IF_y_more_x if_y_more_x_4 (.Y({{26{1'b0}}, CUR_TICK}), .X({32{1'b0}}), .ans(if_y_more_x_4_ans));
  IF_y_eq_x if_y_eq_x_1 (.Y({{26{1'b0}}, CUR_TICK}), .X({32{1'b0}}), .ans(if_y_eq_x_1_ans));
  not not_14 (not_14_out, WAS_RESULT_CALC_FIRST_TICK);
  and and_8 (and_8_out, ENABLE_t, not_13_out);
  or or_4 (or_4_out, if_y_more_x_4_ans, if_y_eq_x_1_ans);
  and and_9 (and_9_out, or_4_out, ENABLE_t, not_14_out);
  not not_15 (not_15_out, and_8_out);
  // Transmission_Gate transmission_11: pin names not known; wires that end beside it: 1'b0, not_15_out, and_8_out, OUT_DATA[15]
  IF_y_eq_x if_y_eq_x_2 (.Y({{26{1'b0}}, CUR_TICK}), .X(32'hb), .ans(if_y_eq_x_2_ans));
  // Transmission_Gate transmission_12: pin names not known; wires that end beside it: 1'b0, if_y_eq_x_2_ans, transmission_12_p3
  // NOT_Gate not_16 has open pins: in=if_y_eq_x_2_ans, out=open
  // NOT_Gate not_17 has open pins: in=if_y_eq_x_2_ans, out=open
  // Transmission_Gate transmission_13: pin names not known; wires that end beside it: 1'b1, if_y_eq_x_2_ans, transmission_12_p3
  // NOT_Gate not_18 has open pins: in=and_8_out, out=open
  // Transmission_Gate #(.width(32)) transmission_14: pin names not known; wires that end beside it: {{27{1'b0}}, EXP}, and_8_out, transmission_14_p3
  // NOT_Gate not_19 has open pins: in=and_8_out, out=open
  // Transmission_Gate #(.width(32)) transmission_15: pin names not known; wires that end beside it: {{22{1'b0}}, MANT}, and_8_out, transmission_15_p3
  not not_20 (not_20_out, and_9_out);
  // Transmission_Gate transmission_16: pin names not known; wires that end beside it: transmission_12_p3, not_20_out, and_9_out, RESULT_t
  FORMAT_MANT_AND_EXP format_mant_and_exp_1 (
    .INP_EXP(transmission_14_p3), .INP_MANT(transmission_15_p3), .ANS_EXP(format_mant_and_exp_1_ans_exp),
    .FORMATTED_MANT(NUMBER_FOR_SQRT));
  // Probe on format_mant_and_exp_1_ans_exp[4:0]
  // Probe on NUMBER_FOR_SQRT
  // Transmission_Gate #(.width(5)) transmission_17: pin names not known; wires that end beside it: format_mant_and_exp_1_ans_exp[4:0], WAS_RESULT_CALC_FIRST_TICK, transmission_17_p3, OUT_DATA[14:10]
  not not_21 (transmission_17_p3, WAS_RESULT_CALC_FIRST_TICK);

  assign IO_DATA_OUT = IO_DATA_IN;
endmodule

module RS (
  input  R,
  input  C,
  input  S,
  output Q,
  output NQ
);

  wire nand_1_out, nand_2_out, nand_4_out, por_1_out;

  nand nand_1 (nand_1_out, S, C);
  nand nand_2 (nand_2_out, C, R);
  POR por_1 (.out(por_1_out));
  nand nand_3 (Q, nand_1_out, NQ);
  nand nand_4 (nand_4_out, Q, nand_2_out);
  or or_1 (NQ, nand_4_out, por_1_out);
endmodule

module Dtrigger1 (
  input  D,
  input  C,
  input  Enabled,
  output Q,
  output NQ
);

  wire and_1_out;

  and and_1 (and_1_out, Enabled, D);
  D_WithoutEnabled d_withoutenabled_1 (.D(and_1_out), .C(C), .Q(Q), .NQ(NQ));
endmodule

module DTrigger2 (
  input  [1:0] D,
  input  C,
  input  Enabled,
  output [1:0] Q,
  output [1:0] NQ
);

  Dtrigger1 dtrigger1_1 (.D(D[0]), .C(C), .Enabled(Enabled), .Q(Q[0]), .NQ(NQ[0]));
  Dtrigger1 dtrigger1_2 (.D(D[1]), .C(C), .Enabled(Enabled), .Q(Q[1]), .NQ(NQ[1]));
endmodule

module DTrigger4 (
  input  [3:0] D,
  input  C,
  input  Enabled,
  output [3:0] Q,
  output [3:0] NQ
);

  DTrigger2 dtrigger2_1 (.D(D[1:0]), .C(C), .Enabled(Enabled), .Q(Q[1:0]), .NQ(NQ[1:0]));
  DTrigger2 dtrigger2_2 (.D(D[3:2]), .C(C), .Enabled(Enabled), .Q(Q[3:2]), .NQ(NQ[3:2]));
endmodule

module DTrigger8 (
  input  [7:0] D,
  input  C,
  input  Enabled,
  output [7:0] Q,
  output [7:0] NQ
);

  DTrigger4 dtrigger4_1 (.D(D[3:0]), .C(C), .Enabled(Enabled), .Q(Q[3:0]), .NQ(NQ[3:0]));
  DTrigger4 dtrigger4_2 (.D(D[7:4]), .C(C), .Enabled(Enabled), .Q(Q[7:4]), .NQ(NQ[7:4]));
endmodule

module DTrigger16 (
  input  [15:0] D,
  input  C,
  input  Enabled,
  output [15:0] Q,
  output [15:0] NQ
);

  DTrigger8 dtrigger8_1 (.D(D[7:0]), .C(C), .Enabled(Enabled), .Q(Q[7:0]), .NQ(NQ[7:0]));
  DTrigger8 dtrigger8_2 (.D(D[15:8]), .C(C), .Enabled(Enabled), .Q(Q[15:8]), .NQ(NQ[15:8]));
endmodule

module DTrigger32 (
  input  [31:0] D,
  input  C,
  input  Enabled,
  output [31:0] Q,
  output [31:0] NQ
);

  DTrigger16 dtrigger16_1 (.D(D[15:0]), .C(C), .Enabled(Enabled), .Q(Q[15:0]), .NQ(NQ[15:0]));
  DTrigger16 dtrigger16_2 (.D(D[31:16]), .C(C), .Enabled(Enabled), .Q(Q[31:16]), .NQ(NQ[31:16]));
endmodule

module SUM1 (
  input  A,
  input  B,
  input  Cin,
  output S,
  output Cout
);

  wire and_1_out, and_2_out, xor_1_out;

  xor xor_1 (xor_1_out, A, B);
  xor xor_2 (S, xor_1_out, Cin);
  and and_1 (and_1_out, xor_1_out, Cin);
  and and_2 (and_2_out, A, B);
  or or_1 (Cout, and_1_out, and_2_out);
endmodule

module SUM2 (
  input  [1:0] A,
  input  [1:0] B,
  input  Cin,
  output [1:0] S,
  output Cout
);

  wire sum1_1_cout;

  SUM1 sum1_1 (.A(A[0]), .B(B[0]), .Cin(Cin), .S(S[0]), .Cout(sum1_1_cout));
  SUM1 sum1_2 (.A(A[1]), .B(B[1]), .Cin(sum1_1_cout), .S(S[1]), .Cout(Cout));
endmodule

module SUM4 (
  input  [3:0] A,
  input  [3:0] B,
  input  Cin,
  output [3:0] S,
  output Cout
);

  wire sum2_1_cout;

  SUM2 sum2_1 (.A(A[1:0]), .B(B[1:0]), .Cin(Cin), .S(S[1:0]), .Cout(sum2_1_cout));
  SUM2 sum2_2 (.A(A[3:2]), .B(B[3:2]), .Cin(sum2_1_cout), .S(S[3:2]), .Cout(Cout));
endmodule

module SUM8 (
  input  [7:0] A,
  input  [7:0] B,
  input  Cin,
  output [7:0] S,
  output Cout
);

  wire sum4_1_cout;

  SUM4 sum4_1 (.A(A[3:0]), .B(B[3:0]), .Cin(Cin), .S(S[3:0]), .Cout(sum4_1_cout));
  SUM4 sum4_2 (.A(A[7:4]), .B(B[7:4]), .Cin(sum4_1_cout), .S(S[7:4]), .Cout(Cout));
endmodule

module SUM16 (
  input  [15:0] A,
  input  [15:0] B,
  input  Cin,
  output [15:0] S,
  output Cout
);

  wire sum8_1_cout;

  SUM8 sum8_1 (.A(A[7:0]), .B(B[7:0]), .Cin(Cin), .S(S[7:0]), .Cout(sum8_1_cout));
  SUM8 sum8_2 (.A(A[15:8]), .B(B[15:8]), .Cin(sum8_1_cout), .S(S[15:8]), .Cout(Cout));
endmodule

module SUM32 (
  input  [31:0] A,
  input  [31:0] B,
  input  Cin,
  output [31:0] S,
  output Cout
);

  wire sum16_1_cout;

  SUM16 sum16_1 (.A(A[15:0]), .B(B[15:0]), .Cin(Cin), .S(S[15:0]), .Cout(sum16_1_cout));
  // Probe on S[15:0]
  SUM16 sum16_2 (.A(A[31:16]), .B(B[31:16]), .Cin(sum16_1_cout), .S(S[31:16]), .Cout(Cout));
endmodule

module Counter (
  input  Enabled,
  input  CLK,
  input  Done,
  output [5:0] CUR_TICK
);

  wire and_1_out, not_1_out;

  not not_1 (not_1_out, Done);
  and and_1 (and_1_out, CLK, not_1_out);
  T t_1 (.CLK(and_1_out), .Enabled(Enabled), .Tick(CUR_TICK[0]));
  T t_2 (.CLK(CUR_TICK[0]), .Enabled(Enabled), .Tick(CUR_TICK[1]));
  T t_3 (.CLK(CUR_TICK[1]), .Enabled(Enabled), .Tick(CUR_TICK[2]));
  T t_4 (.CLK(CUR_TICK[2]), .Enabled(Enabled), .Tick(CUR_TICK[3]));
  T t_5 (.CLK(CUR_TICK[3]), .Enabled(Enabled), .Tick(CUR_TICK[4]));
  T t_6 (.CLK(CUR_TICK[4]), .Enabled(Enabled), .Tick(CUR_TICK[5]));
endmodule

module T (
  input  CLK,
  input  Enabled,
  output Tick
);

  wire old_d_trigger_with_enabled_1_nq;

  OLD_D_TRIGGER_WITH_ENABLED old_d_trigger_with_enabled_1 (
    .D(old_d_trigger_with_enabled_1_nq), .C(CLK), .Enabled(Enabled), .Q(Tick),
    .NQ(old_d_trigger_with_enabled_1_nq));
endmodule

module MINUS32 (
  input  [31:0] A,
  input  [31:0] B,
  output [31:0] S,
  output Cout
);

  wire [31:0] sum32_1_s, xor_1_out;

  assign xor_1_out = {32{1'b1}} ^ B;  // XOR_Gate xor_1, 32 bits wide
  // Probe on xor_1_out
  SUM32 sum32_1 (.A(32'h1), .B(xor_1_out), .S(sum32_1_s));  // open: Cin, Cout
  // Probe on sum32_1_s
  SUM32 sum32_2 (.A(A), .B(sum32_1_s), .S(S), .Cout(Cout));  // open: Cin
endmodule

module COMP1 (
  input  A,
  input  B,
  output EQ,
  output MORE,
  output LESS
);

  wire not_1_out, not_2_out, not_3_out, not_4_out;

  xnor xnor_1 (EQ, A, B);
  not not_1 (not_1_out, EQ);
  not not_2 (not_2_out, B);
  not not_3 (not_3_out, EQ);
  not not_4 (not_4_out, A);
  and and_1 (MORE, not_1_out, not_2_out);
  and and_2 (LESS, not_3_out, not_4_out);
endmodule

module COMP2 (
  input  [1:0] A,
  input  [1:0] B,
  output EQ,
  output MORE,
  output LESS
);

  wire and_2_out, and_3_out, comp1_1_eq, comp1_1_less, comp1_1_more, comp1_2_eq, comp1_2_less, comp1_2_more;

  COMP1 comp1_1 (.A(A[1]), .B(B[1]), .EQ(comp1_1_eq), .MORE(comp1_1_more), .LESS(comp1_1_less));
  COMP1 comp1_2 (.A(A[0]), .B(B[0]), .EQ(comp1_2_eq), .MORE(comp1_2_more), .LESS(comp1_2_less));
  and and_1 (EQ, comp1_1_eq, comp1_2_eq);
  and and_2 (and_2_out, comp1_1_eq, comp1_2_more);
  or or_1 (MORE, comp1_1_more, and_2_out);
  or or_2 (LESS, comp1_1_less, and_3_out);
  and and_3 (and_3_out, comp1_1_eq, comp1_2_less);
endmodule

module COMP4 (
  input  [3:0] A,
  input  [3:0] B,
  output EQ,
  output MORE,
  output LESS
);

  wire and_2_out, and_3_out, comp2_1_eq, comp2_1_less, comp2_1_more, comp2_2_eq, comp2_2_less, comp2_2_more;

  COMP2 comp2_1 (.A(A[3:2]), .B(B[3:2]), .EQ(comp2_1_eq), .MORE(comp2_1_more), .LESS(comp2_1_less));
  COMP2 comp2_2 (.A(A[1:0]), .B(B[1:0]), .EQ(comp2_2_eq), .MORE(comp2_2_more), .LESS(comp2_2_less));
  and and_1 (EQ, comp2_1_eq, comp2_2_eq);
  and and_2 (and_2_out, comp2_1_eq, comp2_2_more);
  or or_1 (MORE, comp2_1_more, and_2_out);
  or or_2 (LESS, comp2_1_less, and_3_out);
  and and_3 (and_3_out, comp2_1_eq, comp2_2_less);
endmodule

module COMP8 (
  input  [7:0] A,
  input  [7:0] B,
  output EQ,
  output MORE,
  output LESS
);

  wire and_2_out, and_3_out, comp4_1_eq, comp4_1_less, comp4_1_more, comp4_2_eq, comp4_2_less, comp4_2_more;

  COMP4 comp4_1 (.A(A[7:4]), .B(B[7:4]), .EQ(comp4_1_eq), .MORE(comp4_1_more), .LESS(comp4_1_less));
  COMP4 comp4_2 (.A(A[3:0]), .B(B[3:0]), .EQ(comp4_2_eq), .MORE(comp4_2_more), .LESS(comp4_2_less));
  and and_1 (EQ, comp4_1_eq, comp4_2_eq);
  and and_2 (and_2_out, comp4_1_eq, comp4_2_more);
  or or_1 (MORE, comp4_1_more, and_2_out);
  or or_2 (LESS, comp4_1_less, and_3_out);
  and and_3 (and_3_out, comp4_1_eq, comp4_2_less);
endmodule

module COMP16 (
  input  [15:0] A,
  input  [15:0] B,
  output EQ,
  output MORE,
  output LESS
);

  wire and_2_out, and_3_out, comp8_1_eq, comp8_1_less, comp8_1_more, comp8_2_eq, comp8_2_less, comp8_2_more;

  COMP8 comp8_1 (.A(A[15:8]), .B(B[15:8]), .EQ(comp8_1_eq), .MORE(comp8_1_more), .LESS(comp8_1_less));
  COMP8 comp8_2 (.A(A[7:0]), .B(B[7:0]), .EQ(comp8_2_eq), .MORE(comp8_2_more), .LESS(comp8_2_less));
  and and_1 (EQ, comp8_1_eq, comp8_2_eq);
  and and_2 (and_2_out, comp8_1_eq, comp8_2_more);
  or or_1 (MORE, comp8_1_more, and_2_out);
  or or_2 (LESS, comp8_1_less, and_3_out);
  and and_3 (and_3_out, comp8_1_eq, comp8_2_less);
endmodule

module COMP32 (
  input  [31:0] A,
  input  [31:0] B,
  output EQ,
  output MORE,
  output LESS
);

  wire and_2_out, and_3_out, comp16_1_eq, comp16_1_less, comp16_1_more, comp16_2_eq, comp16_2_less,
       comp16_2_more;

  COMP16 comp16_1 (.A(A[31:16]), .B(B[31:16]), .EQ(comp16_1_eq), .MORE(comp16_1_more), .LESS(comp16_1_less));
  COMP16 comp16_2 (.A(A[15:0]), .B(B[15:0]), .EQ(comp16_2_eq), .MORE(comp16_2_more), .LESS(comp16_2_less));
  and and_1 (EQ, comp16_1_eq, comp16_2_eq);
  and and_2 (and_2_out, comp16_1_eq, comp16_2_more);
  or or_1 (MORE, comp16_1_more, and_2_out);
  or or_2 (LESS, comp16_1_less, and_3_out);
  and and_3 (and_3_out, comp16_1_eq, comp16_2_less);
endmodule

module RS_WITH_ENABLED (
  input  R,
  input  C,
  input  S,
  input  Enabled,
  output Q,
  output NQ
);

  wire nand_1_out, nand_2_out, nand_4_out, por_1_out;

  nand nand_1 (nand_1_out, S, C);
  nand nand_2 (nand_2_out, C, R);
  POR por_1 (.out(por_1_out));
  nand nand_3 (Q, nand_1_out, NQ);
  nand nand_4 (nand_4_out, Q, nand_2_out);
  or or_1 (NQ, nand_4_out, por_1_out);
endmodule

module JK (
  input  K,
  input  C,
  input  J,
  output Q,
  output NQ
);

  wire and_1_out, and_2_out, not_1_out, not_2_out, not_3_out, rs_1_nq, rs_1_q;

  and and_1 (and_1_out, Q, K);
  and and_2 (and_2_out, J, NQ);
  RS rs_1 (.R(and_1_out), .C(C), .S(and_2_out), .Q(rs_1_q), .NQ(rs_1_nq));
  not not_1 (not_1_out, rs_1_nq);
  not not_2 (not_2_out, C);
  not not_3 (not_3_out, not_1_out);
  RS rs_2 (.R(not_3_out), .C(not_2_out), .S(rs_1_q), .Q(Q), .NQ(NQ));
endmodule

module D_WithoutEnabled (
  input  D,
  input  C,
  output Q,
  output NQ
);

  wire not_1_out;

  not not_1 (not_1_out, D);
  RS rs_1 (.R(not_1_out), .C(C), .S(D), .Q(Q), .NQ(NQ));
endmodule

module IF_y_eq_x (
  input  [31:0] Y,
  input  [31:0] X,
  output ans
);

  // Probe on Y
  COMP32 comp32_1 (.A(Y), .B(X), .EQ(ans));  // open: MORE, LESS
endmodule

module IF_y_more_x (
  input  [31:0] Y,
  input  [31:0] X,
  output ans
);

  wire comp32_1_eq;

  // Probe on Y
  COMP32 comp32_1 (.A(Y), .B(X), .EQ(comp32_1_eq), .MORE(ans));  // open: LESS
endmodule

module IF_y_less_x (
  input  [31:0] Y,
  input  [31:0] X,
  output ans
);

  wire comp32_1_eq;

  // Probe on Y
  COMP32 comp32_1 (.A(Y), .B(X), .EQ(comp32_1_eq), .LESS(ans));  // open: MORE
endmodule

module CHECK_INCORRECT_INP (
  input  [31:0] MANT,
  input  [31:0] EXP,
  input  SIGN,
  output NAN,
  output PINF,
  output NINF,
  output HAS_RESULT,
  output [15:0] OUT_DATA
);

  wire and_4_out, and_5_out, and_6_out, and_8_out, if_y_eq_x_1_ans, if_y_eq_x_2_ans, if_y_eq_x_3_ans,
       if_y_eq_x_4_ans, if_y_eq_x_5_ans, IS_INP_INF, IS_INP_NAN, IS_INP_NEG, IS_INP_ZERO, not_1_out,
       not_2_out, not_3_out, not_4_out, not_5_out, not_6_out, not_7_out, not_8_out, not_9_out, or_2_out,
       or_4_out, transmission_4_p3;
  wire [15:0] transmission_1_p4;

  not not_1 (not_1_out, IS_INP_NAN);
  and and_1 (IS_INP_NEG, SIGN, not_1_out);
  IF_y_eq_x if_y_eq_x_1 (.Y(MANT), .X({32{1'b0}}), .ans(if_y_eq_x_1_ans));
  IF_y_eq_x if_y_eq_x_2 (.Y({32{1'b0}}), .X(EXP), .ans(if_y_eq_x_2_ans));
  and and_2 (IS_INP_ZERO, if_y_eq_x_1_ans, if_y_eq_x_2_ans);
  not not_2 (not_2_out, IS_INP_INF);
  IF_y_eq_x if_y_eq_x_3 (.Y(32'h1f), .X(EXP), .ans(if_y_eq_x_3_ans));
  and and_3 (IS_INP_NAN, not_2_out, if_y_eq_x_3_ans);
  not not_3 (not_3_out, IS_INP_INF);
  not not_4 (not_4_out, IS_INP_ZERO);
  not not_5 (not_5_out, IS_INP_ZERO);
  and and_4 (and_4_out, IS_INP_NEG, not_4_out);
  not not_6 (not_6_out, SIGN);
  and and_5 (and_5_out, IS_INP_NEG, not_3_out, not_5_out);
  not not_7 (not_7_out, SIGN);
  or or_1 (NAN, IS_INP_NAN, and_4_out);
  and and_6 (and_6_out, IS_INP_INF, not_7_out);
  and and_7 (PINF, IS_INP_INF, not_6_out);
  and and_8 (and_8_out, IS_INP_INF, SIGN);
  or or_2 (or_2_out, IS_INP_ZERO, IS_INP_NAN, and_6_out);
  or or_3 (HAS_RESULT, IS_INP_ZERO, IS_INP_NEG, IS_INP_NAN, IS_INP_INF);
  or or_4 (or_4_out, and_8_out, and_5_out);
  not not_8 (not_8_out, or_4_out);
  not not_9 (not_9_out, or_2_out);
  // Transmission_Gate #(.width(16)) transmission_1: pin names not known; wires that end beside it: 16'hfe00, or_4_out, not_8_out, transmission_1_p4
  // Transmission_Gate #(.width(16)) transmission_2: pin names not known; wires that end beside it: {SIGN, EXP[4:0], MANT[9:0]}, or_2_out, not_9_out, transmission_1_p4
  IF_y_eq_x if_y_eq_x_4 (.Y(32'h1f), .X(EXP), .ans(if_y_eq_x_4_ans));
  IF_y_eq_x if_y_eq_x_5 (.Y(MANT), .X({32{1'b0}}), .ans(if_y_eq_x_5_ans));
  and and_9 (IS_INP_INF, if_y_eq_x_5_ans, if_y_eq_x_4_ans);
  // NOT_Gate not_10 has open pins: in=IS_INP_NAN, out=open
  // Transmission_Gate #(.width(16)) transmission_3: pin names not known; wires that end beside it: IS_INP_NAN, OUT_DATA
  // Transmission_Gate #(.width(16)) transmission_4: pin names not known; wires that end beside it: transmission_1_p4, IS_INP_NAN, transmission_4_p3, OUT_DATA
  not not_11 (transmission_4_p3, IS_INP_NAN);

  assign NINF = 1'b0;

  // Other names for the same wires on the sheet: INP_MANT[31:0] = MANT; INP_EXP[31:0] = EXP; INP_SIGN = SIGN
endmodule

module PriorityEncoder1 (
  input  INP_NUMBER,
  output [31:0] POS_OF_LAST_ONE
);


  assign POS_OF_LAST_ONE = {{31{1'b0}}, INP_NUMBER};
endmodule

module PriorityEncoder2 (
  input  [1:0] INP_NUMBER,
  output [31:0] POS_OF_LAST_ONE
);

  wire if_y_more_x_1_ans, not_2_out;
  wire [31:0] priorityencoder1_1_pos_of_last_one, priorityencoder1_2_pos_of_last_one, sum32_1_s;

  PriorityEncoder1 priorityencoder1_1 (
    .INP_NUMBER(INP_NUMBER[1]), .POS_OF_LAST_ONE(priorityencoder1_1_pos_of_last_one));
  // Probe on priorityencoder1_1_pos_of_last_one
  PriorityEncoder1 priorityencoder1_2 (
    .INP_NUMBER(INP_NUMBER[0]), .POS_OF_LAST_ONE(priorityencoder1_2_pos_of_last_one));
  SUM32 sum32_1 (.A(priorityencoder1_1_pos_of_last_one), .B(32'h1), .Cin(1'b0), .S(sum32_1_s));  // open: Cout
  IF_y_more_x if_y_more_x_1 (.Y(priorityencoder1_1_pos_of_last_one), .X({32{1'b0}}), .ans(if_y_more_x_1_ans));
  // NOT_Gate not_1 has open pins: in=if_y_more_x_1_ans, out=open
  not not_2 (not_2_out, if_y_more_x_1_ans);
  // Transmission_Gate #(.width(32)) transmission_1: pin names not known; wires that end beside it: priorityencoder1_2_pos_of_last_one, if_y_more_x_1_ans, POS_OF_LAST_ONE
  // Transmission_Gate #(.width(32)) transmission_2: pin names not known; wires that end beside it: sum32_1_s, not_2_out, if_y_more_x_1_ans, POS_OF_LAST_ONE
endmodule

module PriorityEncoder4 (
  input  [3:0] INP_NUMBER,
  output [31:0] POS_OF_LAST_ONE
);

  wire if_y_more_x_1_ans, not_2_out;
  wire [31:0] priorityencoder2_1_pos_of_last_one, priorityencoder2_2_pos_of_last_one, sum32_1_s;

  PriorityEncoder2 priorityencoder2_1 (
    .INP_NUMBER(INP_NUMBER[3:2]), .POS_OF_LAST_ONE(priorityencoder2_1_pos_of_last_one));
  // Probe on priorityencoder2_1_pos_of_last_one
  PriorityEncoder2 priorityencoder2_2 (
    .INP_NUMBER(INP_NUMBER[1:0]), .POS_OF_LAST_ONE(priorityencoder2_2_pos_of_last_one));
  SUM32 sum32_1 (.A(priorityencoder2_1_pos_of_last_one), .B(32'h2), .Cin(1'b0), .S(sum32_1_s));  // open: Cout
  IF_y_more_x if_y_more_x_1 (.Y(priorityencoder2_1_pos_of_last_one), .X({32{1'b0}}), .ans(if_y_more_x_1_ans));
  // NOT_Gate not_1 has open pins: in=if_y_more_x_1_ans, out=open
  not not_2 (not_2_out, if_y_more_x_1_ans);
  // Transmission_Gate #(.width(32)) transmission_1: pin names not known; wires that end beside it: priorityencoder2_2_pos_of_last_one, if_y_more_x_1_ans, POS_OF_LAST_ONE
  // Transmission_Gate #(.width(32)) transmission_2: pin names not known; wires that end beside it: sum32_1_s, not_2_out, if_y_more_x_1_ans, POS_OF_LAST_ONE
endmodule

module PriorityEncoder8 (
  input  [7:0] INP_NUMBER,
  output [31:0] POS_OF_LAST_ONE
);

  wire if_y_more_x_1_ans, not_2_out;
  wire [31:0] priorityencoder4_1_pos_of_last_one, priorityencoder4_2_pos_of_last_one, sum32_1_s;

  PriorityEncoder4 priorityencoder4_1 (
    .INP_NUMBER(INP_NUMBER[7:4]), .POS_OF_LAST_ONE(priorityencoder4_1_pos_of_last_one));
  // Probe on priorityencoder4_1_pos_of_last_one
  PriorityEncoder4 priorityencoder4_2 (
    .INP_NUMBER(INP_NUMBER[3:0]), .POS_OF_LAST_ONE(priorityencoder4_2_pos_of_last_one));
  SUM32 sum32_1 (.A(priorityencoder4_1_pos_of_last_one), .B(32'h4), .Cin(1'b0), .S(sum32_1_s));  // open: Cout
  IF_y_more_x if_y_more_x_1 (.Y(priorityencoder4_1_pos_of_last_one), .X({32{1'b0}}), .ans(if_y_more_x_1_ans));
  // NOT_Gate not_1 has open pins: in=if_y_more_x_1_ans, out=open
  not not_2 (not_2_out, if_y_more_x_1_ans);
  // Transmission_Gate #(.width(32)) transmission_1: pin names not known; wires that end beside it: priorityencoder4_2_pos_of_last_one, if_y_more_x_1_ans, POS_OF_LAST_ONE
  // Transmission_Gate #(.width(32)) transmission_2: pin names not known; wires that end beside it: sum32_1_s, not_2_out, if_y_more_x_1_ans, POS_OF_LAST_ONE
endmodule

module PriorityEncoder16 (
  input  [15:0] INP_NUMBER,
  output [31:0] POS_OF_LAST_ONE
);

  wire if_y_more_x_1_ans, not_2_out;
  wire [31:0] priorityencoder8_1_pos_of_last_one, priorityencoder8_2_pos_of_last_one, sum32_1_s;

  PriorityEncoder8 priorityencoder8_1 (
    .INP_NUMBER(INP_NUMBER[15:8]), .POS_OF_LAST_ONE(priorityencoder8_1_pos_of_last_one));
  // Probe on priorityencoder8_1_pos_of_last_one
  PriorityEncoder8 priorityencoder8_2 (
    .INP_NUMBER(INP_NUMBER[7:0]), .POS_OF_LAST_ONE(priorityencoder8_2_pos_of_last_one));
  SUM32 sum32_1 (.A(priorityencoder8_1_pos_of_last_one), .B(32'h8), .Cin(1'b0), .S(sum32_1_s));  // open: Cout
  IF_y_more_x if_y_more_x_1 (.Y(priorityencoder8_1_pos_of_last_one), .X({32{1'b0}}), .ans(if_y_more_x_1_ans));
  // NOT_Gate not_1 has open pins: in=if_y_more_x_1_ans, out=open
  not not_2 (not_2_out, if_y_more_x_1_ans);
  // Transmission_Gate #(.width(32)) transmission_1: pin names not known; wires that end beside it: priorityencoder8_2_pos_of_last_one, if_y_more_x_1_ans, POS_OF_LAST_ONE
  // Transmission_Gate #(.width(32)) transmission_2: pin names not known; wires that end beside it: sum32_1_s, not_2_out, if_y_more_x_1_ans, POS_OF_LAST_ONE
endmodule

module PriorityEncoder32 (
  input  [31:0] INP_NUMBER,
  output [31:0] POS_OF_LAST_ONE
);

  wire if_y_more_x_1_ans, not_2_out;
  wire [31:0] priorityencoder16_1_pos_of_last_one, priorityencoder16_2_pos_of_last_one, sum32_1_s;

  PriorityEncoder16 priorityencoder16_1 (
    .INP_NUMBER(INP_NUMBER[31:16]), .POS_OF_LAST_ONE(priorityencoder16_1_pos_of_last_one));
  // Probe on priorityencoder16_1_pos_of_last_one
  PriorityEncoder16 priorityencoder16_2 (
    .INP_NUMBER(INP_NUMBER[15:0]), .POS_OF_LAST_ONE(priorityencoder16_2_pos_of_last_one));
  SUM32 sum32_1 (.A(priorityencoder16_1_pos_of_last_one), .B(32'h10), .Cin(1'b0), .S(sum32_1_s));  // open: Cout
  IF_y_more_x if_y_more_x_1 (.Y(priorityencoder16_1_pos_of_last_one), .X({32{1'b0}}), .ans(if_y_more_x_1_ans));
  // NOT_Gate not_1 has open pins: in=if_y_more_x_1_ans, out=open
  not not_2 (not_2_out, if_y_more_x_1_ans);
  // Transmission_Gate #(.width(32)) transmission_1: pin names not known; wires that end beside it: priorityencoder16_2_pos_of_last_one, if_y_more_x_1_ans, POS_OF_LAST_ONE
  // Transmission_Gate #(.width(32)) transmission_2: pin names not known; wires that end beside it: sum32_1_s, not_2_out, if_y_more_x_1_ans, POS_OF_LAST_ONE
endmodule

module FORMAT_MANT_AND_EXP (
  input  [31:0] INP_EXP,
  input  [31:0] INP_MANT,
  output [31:0] ANS_EXP,
  output [31:0] FORMATTED_MANT
);

  wire and_1_out, and_2_out, if_y_eq_x_1_ans, if_y_eq_x_2_ans, IS_NUMB_NORMAL, not_1_out, not_2_out,
       not_4_out, not_5_out, not_7_out, not_8_out, transmission_3_p3, transmission_3_p4, transmission_5_p3,
       transmission_6_p3;
  wire [0:0] sum32_3_s;
  wire [31:0] INDEX_OF_LAST_ONE_IN_MANT, minus32_1_s, shift_max10bit_1_out_number, sum32_1_s, sum32_2_s,
       transmission_1_p4, transmission_6_p4;
  wire [31:22] transmission_5_p4;

  SUM32 sum32_1 (.A(INP_EXP), .B(32'ha), .S(sum32_1_s));  // open: Cin, Cout
  MINUS32 minus32_1 (.A(32'hb), .B(INDEX_OF_LAST_ONE_IN_MANT), .S(minus32_1_s));  // open: Cout
  not not_1 (not_1_out, IS_NUMB_NORMAL);
  not not_2 (not_2_out, IS_NUMB_NORMAL);
  // Probe on INDEX_OF_LAST_ONE_IN_MANT
  // Probe on minus32_1_s
  // Transmission_Gate #(.width(32)) transmission_1: pin names not known; wires that end beside it: sum32_1_s, IS_NUMB_NORMAL, not_1_out, transmission_1_p4
  // Transmission_Gate #(.width(32)) transmission_2: pin names not known; wires that end beside it: INDEX_OF_LAST_ONE_IN_MANT, not_2_out, transmission_1_p4
  // Probe on transmission_1_p4
  SUM32 sum32_2 (.A(32'h400), .B(INP_MANT), .S(sum32_2_s));  // open: Cin, Cout
  SHIFT_MAX10BIT shift_max10bit_1 (
    .INP_NUMBER(INP_MANT), .SHIFT(minus32_1_s), .OUT_NUMBER(shift_max10bit_1_out_number));
  // Transmission_Gate #(.width(32)) transmission_3: pin names not known; wires that end beside it: shift_max10bit_1_out_number, IS_NUMB_NORMAL, transmission_3_p3, transmission_3_p4
  not not_3 (transmission_3_p3, IS_NUMB_NORMAL);
  // Probe on {ANS_EXP[30:0], sum32_3_s[0]}
  // Probe on sum32_2_s
  not not_4 (not_4_out, IS_NUMB_NORMAL);
  SUM32 sum32_3 (.A(transmission_1_p4), .B(32'h5), .S({ANS_EXP[30:0], sum32_3_s[0]}));  // open: Cin, Cout
  // Probe on ANS_EXP[30:0]
  // Transmission_Gate #(.width(32)) transmission_4: pin names not known; wires that end beside it: not_4_out, IS_NUMB_NORMAL, transmission_3_p4
  // Probe on transmission_3_p4
  // Probe on {1'b0, ANS_EXP[30:0]}
  // Probe on transmission_3_p4
  IF_y_eq_x if_y_eq_x_1 (.Y(INP_EXP), .X({32{1'b0}}), .ans(if_y_eq_x_1_ans));
  PriorityEncoder32 priorityencoder32_1 (.INP_NUMBER(INP_MANT), .POS_OF_LAST_ONE(INDEX_OF_LAST_ONE_IN_MANT));
  not not_5 (not_5_out, transmission_5_p3);
  // Transmission_Gate #(.width(32)) transmission_5: pin names not known; wires that end beside it: transmission_3_p4, not_5_out, transmission_5_p3, {transmission_5_p4, FORMATTED_MANT[31:10]}
  // Transmission_Gate #(.width(32)) transmission_6: pin names not known; wires that end beside it: transmission_3_p4, transmission_5_p3, transmission_6_p3, transmission_6_p4
  not not_6 (transmission_6_p3, transmission_5_p3);
  not not_7 (not_7_out, if_y_eq_x_1_ans);
  and and_1 (and_1_out, INP_EXP[0], not_7_out);
  and and_2 (and_2_out, if_y_eq_x_1_ans, INDEX_OF_LAST_ONE_IN_MANT[0]);
  or or_1 (transmission_5_p3, and_1_out, and_2_out);
  // Probe on {transmission_5_p4, FORMATTED_MANT[31:10]}
  not not_8 (not_8_out, transmission_5_p3);
  // Transmission_Gate #(.width(32)) transmission_7: pin names not known; wires that end beside it: {transmission_6_p4[30:0], 1'b0}, transmission_5_p3, not_8_out, {transmission_5_p4, FORMATTED_MANT[31:10]}
  IF_y_eq_x if_y_eq_x_2 (.Y(INP_EXP), .X({32{1'b0}}), .ans(if_y_eq_x_2_ans));
  not not_9 (IS_NUMB_NORMAL, if_y_eq_x_2_ans);
  // Probe on {FORMATTED_MANT[31:10], {10{1'b0}}}

  assign ANS_EXP[31] = 1'b0;
  assign FORMATTED_MANT[9:0] = {10{1'b0}};
endmodule

module SHIFT_MAX10BIT (
  input  [31:0] INP_NUMBER,
  input  [31:0] SHIFT,
  output [31:0] OUT_NUMBER
);

  wire not_2_out, not_4_out, transmission_1_p3, transmission_1_p4, transmission_5_p4, transmission_7_p3,
       transmission_7_p4;
  wire [31:0] transmission_2_p4, transmission_4_p4, transmission_8_p4, transmission_11_p4;

  // Transmission_Gate #(.width(32)) transmission_1: pin names not known; wires that end beside it: INP_NUMBER, SHIFT[0], transmission_1_p3, transmission_1_p4
  not not_1 (transmission_1_p3, SHIFT[0]);
  // Transmission_Gate #(.width(32)) transmission_2: pin names not known; wires that end beside it: INP_NUMBER, transmission_1_p3, SHIFT[0], transmission_2_p4
  // Transmission_Gate #(.width(32)) transmission_3: pin names not known; wires that end beside it: {transmission_2_p4[30:0], 1'b0}, transmission_1_p3, SHIFT[0], transmission_1_p4
  // Probe on transmission_1_p4
  not not_2 (not_2_out, SHIFT[1]);
  // Transmission_Gate #(.width(32)) transmission_4: pin names not known; wires that end beside it: transmission_1_p4, not_2_out, SHIFT[1], transmission_4_p4
  // Transmission_Gate #(.width(32)) transmission_5: pin names not known; wires that end beside it: transmission_1_p4, SHIFT[1], not_2_out, transmission_5_p4
  // Transmission_Gate #(.width(32)) transmission_6: pin names not known; wires that end beside it: {transmission_4_p4[29:0], 2'b00}, not_2_out, SHIFT[1], transmission_5_p4
  // Probe on transmission_5_p4
  // Transmission_Gate #(.width(32)) transmission_7: pin names not known; wires that end beside it: transmission_5_p4, SHIFT[2], transmission_7_p3, transmission_7_p4
  not not_3 (transmission_7_p3, SHIFT[2]);
  // Transmission_Gate #(.width(32)) transmission_8: pin names not known; wires that end beside it: transmission_5_p4, transmission_7_p3, SHIFT[2], transmission_8_p4
  // Transmission_Gate #(.width(32)) transmission_9: pin names not known; wires that end beside it: {transmission_8_p4[27:0], 4'b0000}, transmission_7_p3, SHIFT[2], transmission_7_p4
  // Probe on transmission_7_p4
  not not_4 (not_4_out, SHIFT[3]);
  // Transmission_Gate #(.width(32)) transmission_10: pin names not known; wires that end beside it: transmission_7_p4, SHIFT[3], not_4_out, OUT_NUMBER
  // Transmission_Gate #(.width(32)) transmission_11: pin names not known; wires that end beside it: transmission_7_p4, not_4_out, SHIFT[3], transmission_11_p4
  // Transmission_Gate #(.width(32)) transmission_12: pin names not known; wires that end beside it: {transmission_11_p4[23:0], {8{1'b0}}}, not_4_out, SHIFT[3], OUT_NUMBER
  // Probe on OUT_NUMBER
endmodule

module INT32_SQRT_ALGO (
  input  [31:0] INP_NUMBER,
  input  CLK,
  input  ENABLE,
  input  [31:0] CUR_TICK,
  output [31:0] OUT_NUMBER
);

  wire and_1_out, and_2_out, and_3_out, if_y_eq_x_1_ans, if_y_eq_x_2_ans, if_y_eq_x_3_ans, if_y_more_x_1_ans,
       not_1_out, not_2_out, not_3_out, not_4_out, not_5_out, not_6_out, not_7_out, not_10_out,
       transmission_5_p3, transmission_6_p3, transmission_7_p3, transmission_8_p3, transmission_9_p3,
       transmission_10_p3;
  wire [1:0] shift_max10bit_3_out_number;
  wire [31:0] CUR_NUMBER, CUR_ROOT, dtrigger32_1_q, dtrigger32_3_q, dtrigger32_4_q, minus32_1_s,
       NEW_REMAINDER, NEW_ROOT_q, REMAINDER, REMAINDRER_q, shift_max10bit_1_out_number,
       shift_max10bit_2_out_number, shift_max10bit_4_out_number, shift_max10bit_5_out_number, sum32_2_s,
       TMP_BIG_ROOT, transmission_2_p1;
  wire [31:2] TMP_BIG_REMAINDER;

  // Probe on CUR_NUMBER
  // Probe on shift_max10bit_1_out_number
  not not_1 (not_1_out, CLK);
  // Probe on dtrigger32_1_q
  DTrigger32 dtrigger32_1 (
    .D(shift_max10bit_1_out_number), .C(not_1_out), .Enabled(ENABLE), .Q(dtrigger32_1_q));  // open: NQ
  not not_2 (not_2_out, CLK);
  IF_y_eq_x if_y_eq_x_1 (.Y(CUR_TICK), .X(32'h1), .ans(if_y_eq_x_1_ans));
  SHIFT_MAX10BIT shift_max10bit_1 (.INP_NUMBER(CUR_NUMBER), .SHIFT(32'h2), .OUT_NUMBER(shift_max10bit_1_out_number));
  and and_1 (and_1_out, if_y_eq_x_1_ans, ENABLE);
  not not_3 (not_3_out, and_1_out);
  not not_4 (not_4_out, and_1_out);
  // Transmission_Gate #(.width(32)) transmission_1: pin names not known; wires that end beside it: INP_NUMBER, and_1_out, not_3_out, CUR_NUMBER
  // Transmission_Gate #(.width(32)) transmission_2: pin names not known; wires that end beside it: transmission_2_p1, and_1_out, not_4_out, CUR_NUMBER
  DTrigger32 dtrigger32_2 (.D(dtrigger32_1_q), .C(CLK), .Enabled(ENABLE), .Q(transmission_2_p1));  // open: NQ
  // Probe on transmission_2_p1
  DTrigger32 dtrigger32_3 (.D(NEW_REMAINDER), .C(not_2_out), .Enabled(ENABLE), .Q(dtrigger32_3_q));  // open: NQ
  IF_y_eq_x if_y_eq_x_2 (.Y(CUR_TICK), .X(32'h1), .ans(if_y_eq_x_2_ans));
  // Probe on OUT_NUMBER
  // Probe on CUR_NUMBER
  and and_2 (and_2_out, if_y_eq_x_2_ans, ENABLE);
  not not_5 (not_5_out, and_2_out);
  not not_6 (not_6_out, and_2_out);
  DTrigger32 REMAINDRER (.D(dtrigger32_3_q), .C(CLK), .Enabled(ENABLE), .Q(REMAINDRER_q));  // open: NQ
  // Transmission_Gate #(.width(32)) transmission_3: pin names not known; wires that end beside it: {32{1'b0}}, and_2_out, not_5_out, REMAINDER
  // Transmission_Gate #(.width(32)) transmission_4: pin names not known; wires that end beside it: REMAINDRER_q, and_2_out, not_6_out, REMAINDER
  not not_7 (not_7_out, CLK);
  // Probe on REMAINDER
  DTrigger32 dtrigger32_4 (.D(OUT_NUMBER), .C(not_7_out), .Enabled(ENABLE), .Q(dtrigger32_4_q));  // open: NQ
  IF_y_eq_x if_y_eq_x_3 (.Y(CUR_TICK), .X(32'h1), .ans(if_y_eq_x_3_ans));
  and and_3 (and_3_out, if_y_eq_x_3_ans, ENABLE);
  DTrigger32 NEW_ROOT (.D(dtrigger32_4_q), .C(CLK), .Enabled(ENABLE), .Q(NEW_ROOT_q));  // open: NQ
  // Transmission_Gate #(.width(32)) transmission_5: pin names not known; wires that end beside it: {32{1'b0}}, and_3_out, transmission_5_p3, CUR_ROOT
  not not_8 (transmission_5_p3, and_3_out);
  // Transmission_Gate #(.width(32)) transmission_6: pin names not known; wires that end beside it: NEW_ROOT_q, and_3_out, transmission_6_p3, CUR_ROOT
  not not_9 (transmission_6_p3, and_3_out);
  // Probe on shift_max10bit_2_out_number
  // Probe on CUR_NUMBER[21:20]
  SHIFT_MAX10BIT shift_max10bit_2 (.INP_NUMBER(CUR_ROOT), .SHIFT(32'h2), .OUT_NUMBER(shift_max10bit_2_out_number));
  SHIFT_MAX10BIT shift_max10bit_3 (
    .INP_NUMBER(REMAINDER), .SHIFT(32'h2), .OUT_NUMBER({TMP_BIG_REMAINDER, shift_max10bit_3_out_number}));
  // Probe on TMP_BIG_ROOT
  SUM32 sum32_1 (.A(shift_max10bit_2_out_number), .B(32'h1), .S(TMP_BIG_ROOT));  // open: Cin, Cout
  SHIFT_MAX10BIT shift_max10bit_4 (.INP_NUMBER(CUR_ROOT), .SHIFT(32'h1), .OUT_NUMBER(shift_max10bit_4_out_number));
  IF_y_more_x if_y_more_x_1 (.Y(TMP_BIG_ROOT), .X({TMP_BIG_REMAINDER, CUR_NUMBER[21:20]}), .ans(if_y_more_x_1_ans));
  SHIFT_MAX10BIT shift_max10bit_5 (.INP_NUMBER(CUR_ROOT), .SHIFT(32'h1), .OUT_NUMBER(shift_max10bit_5_out_number));
  MINUS32 minus32_1 (.A({TMP_BIG_REMAINDER, CUR_NUMBER[21:20]}), .B(TMP_BIG_ROOT), .S(minus32_1_s));  // open: Cout
  not not_10 (not_10_out, if_y_more_x_1_ans);
  // Transmission_Gate #(.width(32)) transmission_7: pin names not known; wires that end beside it: shift_max10bit_5_out_number, not_10_out, transmission_7_p3, OUT_NUMBER
  not not_11 (transmission_7_p3, not_10_out);
  // Transmission_Gate #(.width(32)) transmission_8: pin names not known; wires that end beside it: {TMP_BIG_REMAINDER, CUR_NUMBER[21:20]}, not_10_out, transmission_8_p3, NEW_REMAINDER
  not not_12 (transmission_8_p3, not_10_out);
  SUM32 sum32_2 (.A(shift_max10bit_4_out_number), .B(32'h1), .S(sum32_2_s));  // open: Cin, Cout
  // Transmission_Gate #(.width(32)) transmission_9: pin names not known; wires that end beside it: sum32_2_s, not_10_out, transmission_9_p3, OUT_NUMBER
  not not_13 (transmission_9_p3, not_10_out);
  // Transmission_Gate #(.width(32)) transmission_10: pin names not known; wires that end beside it: minus32_1_s, not_10_out, transmission_10_p3, NEW_REMAINDER
  not not_14 (transmission_10_p3, not_10_out);
  // Probe on OUT_NUMBER
  // Probe on NEW_REMAINDER

  // Other names for the same wires on the sheet: NEW_ROOT[31:0] = OUT_NUMBER;
  //   TMP_BIG_REMAINDER[1:0] = CUR_NUMBER[21:20]

  // Notes on the sheet:
  //   Это итерация алгоритма
endmodule

module DtriggerOnJK (
  input  D,
  input  C,
  output Q,
  output NQ
);

  wire not_1_out;

  not not_1 (not_1_out, D);
  JK jk_1 (.K(not_1_out), .C(C), .J(D), .Q(Q), .NQ(NQ));
endmodule

module DTriggerOnJkEnabled (
  input  D,
  input  C,
  input  Enabled,
  output Q,
  output NQ
);

  wire and_1_out;

  and and_1 (and_1_out, Enabled, D);
  DtriggerOnJK dtriggeronjk_1 (.D(and_1_out), .C(C), .Q(Q), .NQ(NQ));
endmodule

module OLD_RS_WITH_ENABLED (
  input  R,
  input  C,
  input  S,
  input  Enabled,
  output Q,
  output NQ
);

  wire and_1_out, nand_1_out, nand_2_out, nand_3_out, nand_4_out, or_1_out, por_1_out;

  nand nand_1 (nand_1_out, S, C);
  nand nand_2 (nand_2_out, C, R);
  POR por_1 (.out(por_1_out));
  nand nand_3 (nand_3_out, nand_1_out, or_1_out);
  nand nand_4 (nand_4_out, and_1_out, nand_2_out);
  and and_1 (and_1_out, Enabled, nand_3_out);
  or or_1 (or_1_out, nand_4_out, por_1_out);
  and and_2 (Q, Enabled, and_1_out);
  not not_1 (NQ, Q);
endmodule

module OLD_JK_WITH_ENABLED (
  input  K,
  input  C,
  input  J,
  input  Enabled,
  output Q,
  output NQ
);

  wire and_1_out, and_2_out, not_1_out, not_2_out, not_3_out, old_rs_with_enabled_1_nq,
       old_rs_with_enabled_1_q;

  and and_1 (and_1_out, Q, K);
  and and_2 (and_2_out, J, NQ);
  OLD_RS_WITH_ENABLED old_rs_with_enabled_1 (
    .R(and_1_out), .C(C), .S(and_2_out), .Enabled(Enabled), .Q(old_rs_with_enabled_1_q),
    .NQ(old_rs_with_enabled_1_nq));
  not not_1 (not_1_out, old_rs_with_enabled_1_nq);
  not not_2 (not_2_out, C);
  not not_3 (not_3_out, not_1_out);
  RS rs_1 (.R(not_3_out), .C(not_2_out), .S(old_rs_with_enabled_1_q), .Q(Q), .NQ(NQ));
endmodule

module OLD_D_TRIGGER_WITH_ENABLED (
  input  D,
  input  C,
  input  Enabled,
  output Q,
  output NQ
);

  wire not_1_out;

  not not_1 (not_1_out, D);
  OLD_JK_WITH_ENABLED old_jk_with_enabled_1 (.K(not_1_out), .C(C), .J(D), .Enabled(Enabled), .Q(Q), .NQ(NQ));
endmodule
